# Fritzing sketch tinyfox_layout (saved by Fritzing 0.8.5b)
circuit board: 8.46667cm x 5.64444cm
breadboards: 1
perfboards: 1

parts:
  R2 = Resistor [tolerance=±5% resistance=2k package=THT]
  U1 = attiny85 [package=dip]
  BIG_(3_5mm) = Header 3 [package=screwterminal-3.5mm-3_lock.007s]
  SMALL_(2_5mm) = Header 3 [package=screwterminal-3.5mm-3_lock.007s]
  R1 = Resistor [tolerance=±5% resistance=2k package=THT]

nets:
  N1: R2.Pin_0, U1.Pin_3, BIG_(3_5mm).3
  N2: R2.Pin_1, BIG_(3_5mm).2, R1.Pin_0
  N3: U1.Pin_2, R1.Pin_1
  N4: U1.Pin_4, SMALL_(2_5mm).3
  N5: U1.Pin_8, BIG_(3_5mm).1

notes:
  sleeve
  ring
  tip
